// Logisim project ObligatorioARQ.circ as structural Verilog: 4 circuits, main circuit main
module main (
  input  [11:0] in_1
);

  wire and_1_out, and_2_out, and_3_out, and_4_out, and_5_out, button_1_out, button_2_out, button_3_out,
       button_4_out, button_5_out, button_6_out, button_7_out, contadorpuntosbinario_1_led1,
       contadorpuntosbinario_1_led2, contadorpuntosbinario_1_led3, contadorpuntosbinario_1_led4,
       contadorpuntosbinario_1_led5, contadorpuntosbinario_1_led6, contadorpuntosbinario_1_led7,
       contadorpuntosbinario_1_led8, contadortiempo_1_reset, d_ff_1_q, decoder_1_out2, decoder_1_out3,
       decoder_1_out4, decoder_1_out5, grabacioncuadrados_1_pinluzgrabando,
       grabacioncuadrados_1_pinluzjugando, nor_1_out, or_1_out, or_2_out, RelojMatriz_out;
  wire [2:0] undriven;
  wire [3:0] contadortiempo_1_mins, contadortiempo_1_segs, contadortiempo_1_segs2;
  wire [11:0] shift_register_1_out, shift_register_2_out, shift_register_3_out, shift_register_4_out;

  or or_1 (or_1_out, grabacioncuadrados_1_pinluzgrabando, d_ff_1_q);
  nor nor_1 (nor_1_out, grabacioncuadrados_1_pinluzgrabando, grabacioncuadrados_1_pinluzjugando, d_ff_1_q);
  D_Flip_Flop d_ff_1 (.Q(d_ff_1_q), .preset(button_1_out), .reset(contadortiempo_1_reset));  // open: D, clk, Qn
  LED led_1 (.in(nor_1_out));
  LED led_2 (.in(or_1_out));
  LED led_3 (.in(grabacioncuadrados_1_pinluzjugando));
  Clock RelojMatriz (.out(RelojMatriz_out));
  Random #(.width(3)) RNG ();  // open: clk, next, out, clr
  and and_1 (and_1_out, d_ff_1_q, RelojMatriz_out);
  Decoder #(.select(3)) decoder_1 (
    .out2(decoder_1_out2), .out3(decoder_1_out3), .out4(decoder_1_out4), .out5(decoder_1_out5), .sel(undriven));  // open: out0, out1, out6, out7, en
  Button button_1 (.out(button_1_out));
  Button button_2 (.out(button_2_out));
  Button button_3 (.out(button_3_out));
  grabacionCuadrados grabacioncuadrados_1 (
    .EntradaBotonGrabar(button_3_out), .EntradaJugarGrabacion(button_2_out),
    .PinLuzJugando(grabacioncuadrados_1_pinluzjugando), .PinLuzGrabando(grabacioncuadrados_1_pinluzgrabando));  // open: Columna1, Columna2, Columna3, Columna4
  Shift_Register #(.length(12)) shift_register_1 (
    .in(decoder_1_out2), .clk(and_1_out), .out(shift_register_1_out[0]), .clr(contadortiempo_1_reset),
    .q0(shift_register_1_out[11]), .q1(shift_register_1_out[10]), .q2(shift_register_1_out[9]),
    .q3(shift_register_1_out[8]), .q4(shift_register_1_out[7]), .q5(shift_register_1_out[6]),
    .q6(shift_register_1_out[5]), .q7(shift_register_1_out[4]), .q8(shift_register_1_out[3]),
    .q9(shift_register_1_out[2]), .q10(shift_register_1_out[1]));  // open: shift, load, d0, d1, d2, d3, d4, d5, d6, d7, d8, d9, d10, d11, q11
  Shift_Register #(.length(12)) shift_register_2 (
    .in(decoder_1_out3), .clk(and_1_out), .out(shift_register_2_out[0]), .clr(contadortiempo_1_reset),
    .q0(shift_register_2_out[11]), .q1(shift_register_2_out[10]), .q2(shift_register_2_out[9]),
    .q3(shift_register_2_out[8]), .q4(shift_register_2_out[7]), .q5(shift_register_2_out[6]),
    .q6(shift_register_2_out[5]), .q7(shift_register_2_out[4]), .q8(shift_register_2_out[3]),
    .q9(shift_register_2_out[2]), .q10(shift_register_2_out[1]));  // open: shift, load, d0, d1, d2, d3, d4, d5, d6, d7, d8, d9, d10, d11, q11
  Shift_Register #(.length(12)) shift_register_3 (
    .in(decoder_1_out4), .clk(and_1_out), .out(shift_register_3_out[0]), .clr(contadortiempo_1_reset),
    .q0(shift_register_3_out[11]), .q1(shift_register_3_out[10]), .q2(shift_register_3_out[9]),
    .q3(shift_register_3_out[8]), .q4(shift_register_3_out[7]), .q5(shift_register_3_out[6]),
    .q6(shift_register_3_out[5]), .q7(shift_register_3_out[4]), .q8(shift_register_3_out[3]),
    .q9(shift_register_3_out[2]), .q10(shift_register_3_out[1]));  // open: shift, load, d0, d1, d2, d3, d4, d5, d6, d7, d8, d9, d10, d11, q11
  Shift_Register #(.length(12)) shift_register_4 (
    .in(decoder_1_out5), .clk(and_1_out), .out(shift_register_4_out[0]), .clr(contadortiempo_1_reset),
    .q0(shift_register_4_out[11]), .q1(shift_register_4_out[10]), .q2(shift_register_4_out[9]),
    .q3(shift_register_4_out[8]), .q4(shift_register_4_out[7]), .q5(shift_register_4_out[6]),
    .q6(shift_register_4_out[5]), .q7(shift_register_4_out[4]), .q8(shift_register_4_out[3]),
    .q9(shift_register_4_out[2]), .q10(shift_register_4_out[1]));  // open: shift, load, d0, d1, d2, d3, d4, d5, d6, d7, d8, d9, d10, d11, q11
  DotMatrix #(.matrixcols(9), .matrixrows(12)) dotmatrix_1 (
    .col0(in_1), .col1(shift_register_1_out), .col2(in_1), .col3(shift_register_2_out), .col4(in_1),
    .col5(shift_register_3_out), .col6(in_1), .col7(shift_register_4_out), .col8(in_1));
  Hex_Digit_Display hex_digit_display_1 (.value(contadortiempo_1_mins));  // open: dp
  Button button_4 (.out(button_4_out));
  and and_2 (and_2_out, button_4_out, shift_register_1_out[2]);
  and and_3 (and_3_out, button_5_out, shift_register_2_out[2]);
  and and_4 (and_4_out, button_6_out, shift_register_3_out[2]);
  and and_5 (and_5_out, button_7_out, shift_register_4_out[2]);
  Hex_Digit_Display hex_digit_display_2 (.value(contadortiempo_1_segs2));  // open: dp
  Button button_5 (.out(button_5_out));
  Button button_6 (.out(button_6_out));
  Button button_7 (.out(button_7_out));
  Hex_Digit_Display hex_digit_display_3 (.value(contadortiempo_1_segs));  // open: dp
  ContadorPuntosBinario contadorpuntosbinario_1 (
    .ENTRADA(or_2_out), .RESET(button_1_out), .Led1(contadorpuntosbinario_1_led1),
    .Led2(contadorpuntosbinario_1_led2), .Led3(contadorpuntosbinario_1_led3),
    .Led4(contadorpuntosbinario_1_led4), .Led5(contadorpuntosbinario_1_led5),
    .Led6(contadorpuntosbinario_1_led6), .Led7(contadorpuntosbinario_1_led7),
    .Led8(contadorpuntosbinario_1_led8));
  LED led_4 (.in(contadorpuntosbinario_1_led8));
  LED led_5 (.in(contadorpuntosbinario_1_led7));
  LED led_6 (.in(contadorpuntosbinario_1_led6));
  LED led_7 (.in(contadorpuntosbinario_1_led5));
  or or_2 (or_2_out, and_2_out, and_3_out, and_4_out, and_5_out);
  LED led_8 (.in(contadorpuntosbinario_1_led4));
  LED led_9 (.in(contadorpuntosbinario_1_led3));
  LED led_10 (.in(contadorpuntosbinario_1_led2));
  LED led_11 (.in(contadorpuntosbinario_1_led1));
  ContadorTiempo contadortiempo_1 (
    .in_1(and_1_out), .Mins(contadortiempo_1_mins), .Segs2(contadortiempo_1_segs2),
    .Segs(contadortiempo_1_segs), .Reset(contadortiempo_1_reset));

  // Notes on the sheet:
  //   Esperando modo
  //   Jugando
  //   Grabando
  //   Grabar
  //   Jugar random
  //   Jugar grabacion
  //   ORTquestra
  //   ____
  //   :
  //   Contador puntos en binario:
endmodule

module ContadorTiempo (
  input  in_1,
  output [3:0] Mins,
  output [3:0] Segs2,
  output [3:0] Segs,
  output Reset
);

  wire and_1_out, clock_1_out, counter_2_carry, counter_3_carry, d_ff_1_q;

  Clock clock_1 (.out(clock_1_out));
  D_Flip_Flop d_ff_1 (.Q(d_ff_1_q), .preset(in_1), .reset(Reset));  // open: D, clk, Qn
  and and_1 (and_1_out, d_ff_1_q, clock_1_out);
  Counter #(.max('h2), .trigger("falling"), .width(4)) counter_1 (
    .clr(Reset), .clk(counter_2_carry), .carry(Reset), .Q(Mins));  // open: load, up, count, D
  Counter #(.max('h5), .trigger("falling"), .width(4)) counter_2 (
    .clr(Reset), .clk(counter_3_carry), .carry(counter_2_carry), .Q(Segs2));  // open: load, up, count, D
  Counter #(.max('h9), .width(4)) counter_3 (
    .clr(Reset), .clk(and_1_out), .carry(counter_3_carry), .Q(Segs));  // open: load, up, count, D
endmodule

module ContadorPuntosBinario (
  input  ENTRADA,
  input  RESET,
  output Led1,
  output Led2,
  output Led3,
  output Led4,
  output Led5,
  output Led6,
  output Led7,
  output Led8
);

  wire and_1_out, and_2_out, and_3_out, and_4_out, and_5_out, and_6_out;

  J_K_Flip_Flop j_k_ff_1 (.J(ENTRADA), .K(ENTRADA), .clk(ENTRADA), .Q(Led1), .reset(RESET));  // open: Qn, preset
  and and_1 (and_1_out, Led1, Led2);
  J_K_Flip_Flop j_k_ff_2 (.J(Led1), .K(Led1), .clk(ENTRADA), .Q(Led2), .reset(RESET));  // open: Qn, preset
  and and_2 (and_2_out, and_1_out, Led3);
  J_K_Flip_Flop j_k_ff_3 (.J(and_1_out), .K(and_1_out), .clk(ENTRADA), .Q(Led3), .reset(RESET));  // open: Qn, preset
  J_K_Flip_Flop j_k_ff_4 (.J(and_2_out), .K(and_2_out), .clk(ENTRADA), .Q(Led4), .reset(RESET));  // open: Qn, preset
  and and_3 (and_3_out, and_2_out, Led4);
  J_K_Flip_Flop j_k_ff_5 (.J(and_3_out), .K(and_3_out), .clk(ENTRADA), .Q(Led5), .reset(RESET));  // open: Qn, preset
  and and_4 (and_4_out, and_3_out, Led5);
  and and_5 (and_5_out, and_4_out, Led6);
  J_K_Flip_Flop j_k_ff_6 (.J(and_4_out), .K(and_4_out), .clk(ENTRADA), .Q(Led6), .reset(RESET));  // open: Qn, preset
  and and_6 (and_6_out, and_5_out, Led7);
  J_K_Flip_Flop j_k_ff_7 (.J(and_5_out), .K(and_5_out), .clk(ENTRADA), .Q(Led7), .reset(RESET));  // open: Qn, preset
  J_K_Flip_Flop j_k_ff_8 (.J(and_6_out), .K(and_6_out), .clk(ENTRADA), .Q(Led8), .reset(RESET));  // open: Qn, preset
endmodule

module grabacionCuadrados (
  input  EntradaBotonGrabar,
  input  EntradaJugarGrabacion,
  output Columna1,
  output Columna2,
  output Columna3,
  output Columna4,
  output PinLuzJugando,
  output PinLuzGrabando
);

  wire and_1_out, clock_1_out, decoder_1_out2, decoder_1_out3, decoder_1_out4, decoder_1_out5, undriven_2;
  wire [2:0] undriven;
  wire [3:0] ram_1_dout;
  wire [4:0] counter_1_q;
  wire [11:0] shift_register_3_out, shift_register_4_out;
  wire [11:1] shift_register_1_q10, shift_register_2_q10;

  Random #(.width(3)) random_1 ();  // open: clk, next, out, clr
  and and_1 (and_1_out, clock_1_out, PinLuzGrabando);
  J_K_Flip_Flop j_k_ff_1 (
    .J(EntradaBotonGrabar), .K(EntradaBotonGrabar), .clk(EntradaBotonGrabar), .Q(PinLuzGrabando));  // open: Qn, preset, reset
  Decoder #(.select(3)) decoder_1 (
    .out2(decoder_1_out2), .out3(decoder_1_out3), .out4(decoder_1_out4), .out5(decoder_1_out5), .sel(undriven));  // open: out0, out1, out6, out7, en
  Shift_Register #(.length(12)) shift_register_1 (
    .in(decoder_1_out2), .clk(clock_1_out), .load(EntradaBotonGrabar), .clr(EntradaBotonGrabar),
    .q0(shift_register_1_q10[11]), .q1(shift_register_1_q10[10]), .q2(shift_register_1_q10[9]),
    .q3(shift_register_1_q10[8]), .q4(shift_register_1_q10[7]), .q5(shift_register_1_q10[6]),
    .q6(shift_register_1_q10[5]), .q7(shift_register_1_q10[4]), .q8(shift_register_1_q10[3]),
    .q9(shift_register_1_q10[2]), .q10(shift_register_1_q10[1]));  // open: shift, out, d0, d1, d2, d3, d4, d5, d6, d7, d8, d9, d10, d11, q11
  Shift_Register #(.length(12)) shift_register_2 (
    .in(decoder_1_out3), .clk(clock_1_out), .load(EntradaBotonGrabar), .clr(EntradaBotonGrabar),
    .q0(shift_register_2_q10[11]), .q1(shift_register_2_q10[10]), .q2(shift_register_2_q10[9]),
    .q3(shift_register_2_q10[8]), .q4(shift_register_2_q10[7]), .q5(shift_register_2_q10[6]),
    .q6(shift_register_2_q10[5]), .q7(shift_register_2_q10[4]), .q8(shift_register_2_q10[3]),
    .q9(shift_register_2_q10[2]), .q10(shift_register_2_q10[1]));  // open: shift, out, d0, d1, d2, d3, d4, d5, d6, d7, d8, d9, d10, d11, q11
  Shift_Register #(.length(12)) shift_register_3 (
    .in(decoder_1_out4), .clk(clock_1_out), .out(shift_register_3_out[0]), .load(EntradaBotonGrabar),
    .clr(EntradaBotonGrabar), .q0(shift_register_3_out[11]), .q1(shift_register_3_out[10]),
    .q2(shift_register_3_out[9]), .q3(shift_register_3_out[8]), .q4(shift_register_3_out[7]),
    .q5(shift_register_3_out[6]), .q6(shift_register_3_out[5]), .q7(shift_register_3_out[4]),
    .q8(shift_register_3_out[3]), .q9(shift_register_3_out[2]), .q10(shift_register_3_out[1]));  // open: shift, d0, d1, d2, d3, d4, d5, d6, d7, d8, d9, d10, d11, q11
  Shift_Register #(.length(12)) shift_register_4 (
    .in(decoder_1_out5), .clk(clock_1_out), .out(shift_register_4_out[0]), .load(EntradaBotonGrabar),
    .clr(EntradaBotonGrabar), .q0(shift_register_4_out[11]), .q1(shift_register_4_out[10]),
    .q2(shift_register_4_out[9]), .q3(shift_register_4_out[8]), .q4(shift_register_4_out[7]),
    .q5(shift_register_4_out[6]), .q6(shift_register_4_out[5]), .q7(shift_register_4_out[4]),
    .q8(shift_register_4_out[3]), .q9(shift_register_4_out[2]), .q10(shift_register_4_out[1]));  // open: shift, d0, d1, d2, d3, d4, d5, d6, d7, d8, d9, d10, d11, q11
  Clock clock_1 (.out(clock_1_out));
  Counter #(.max('h1f), .width(5)) counter_1 (
    .Q(counter_1_q), .clk(clock_1_out));  // open: load, D, count, carry, up, clr
  RAM #(.addrWidth(5), .dataWidth(4)) ram_1 (
    .addr(counter_1_q), .we(PinLuzGrabando), .oe(undriven_2), .clk(clock_1_out),
    .din({shift_register_4_out[11], shift_register_3_out[11], shift_register_2_q10[11], shift_register_1_q10[11]}),
    .dout(ram_1_dout));
  J_K_Flip_Flop j_k_ff_2 (
    .J(EntradaJugarGrabacion), .K(EntradaJugarGrabacion), .clk(EntradaJugarGrabacion), .Q(PinLuzJugando));  // open: Qn, preset, reset
endmodule
